// Logisim project Cache.circ as structural Verilog: 7 circuits, main circuit main
module main (
  input  EnableTestHalting,
  output [9:0] CorrectCounter,
  output [9:0] HitCounter,
  output [9:0] MissCounter,
  output [9:0] TestNumber,
  output [7:0] ByteRead,
  output [7:0] CorrectByteRead,
  output Halt
);

  wire and_3_out, and_4_out, and_5_out, CLK, CmdIsRead, Correct, CpuRead, CpuWrite, DidContain, HaltTesting,
       MaxItersReached, MemRead, MemWrite, not_1_out, not_2_out, not_4_out, NotDoneTesting, Ok2Count,
       or_1_out, Ready;
  wire [7:0] CpuWriteValue, MemAddress;
  wire [9:0] CpuAddress;
  wire [31:0] Line2Mem, LineFromMem;

  not not_1 (not_1_out, Ready);
  Clock clock_1 (.out(CLK));
  or or_1 (or_1_out, MaxItersReached, Ready);
  Counter #(.width(4), .max('h9)) MaxClocks (
    .load(Ready), .D(4'b0001), .count(not_1_out), .carry(MaxItersReached), .clk(CLK));  // open: Q, clr
  and and_1 (HaltTesting, EnableTestHalting, CmdIsRead, not_2_out);
  not not_2 (not_2_out, Correct);
  not not_3 (NotDoneTesting, Halt);
  Inputs inputs_1 (
    .HaltTesting(HaltTesting), .Ready(or_1_out), .CLK(CLK), .Done(Halt), .Read(CpuRead), .Write(CpuWrite),
    .Address(CpuAddress), .Value(CpuWriteValue), .TestNumber(TestNumber));
  Cache cache_1 (
    .CpuAddress(CpuAddress), .CpuRead(CpuRead), .CpuWrite(CpuWrite), .CpuWriteValue(CpuWriteValue),
    .CLK(CLK), .Ready(Ready), .DidContain(DidContain), .ByteRead(ByteRead), .MemAddress(MemAddress),
    .MemRead(MemRead), .MemWrite(MemWrite), .Line2Mem(Line2Mem), .LineFromMem(LineFromMem));
  // Probe on CpuRead
  // Probe on CpuWrite
  // Probe on CpuAddress
  // Probe on CpuWriteValue
  // Probe on TestNumber
  // Probe on CorrectByteRead
  // Probe on Correct
  // Probe on Ready
  // Probe on DidContain
  // Probe on ByteRead
  // Probe on MemAddress
  // Probe on MemRead
  // Probe on MemWrite
  // Probe on HitCounter
  // Probe on LineFromMem
  // Probe on Line2Mem
  not not_4 (not_4_out, HaltTesting);
  RAM #(.dataWidth(32), .bus("separate")) ram_1 (
    .addr(MemAddress), .din(Line2Mem), .data(LineFromMem), .str(MemWrite), .clk(CLK), .ld(MemRead));  // open: sel, clr
  and and_2 (Ok2Count, Ready, not_4_out, NotDoneTesting);
  and and_3 (and_3_out, Correct, Ok2Count);
  and and_4 (and_4_out, DidContain, Ok2Count);
  and and_5 (and_5_out, MemRead, NotDoneTesting);
  Checker checker_1 (
    .TestNumber(TestNumber), .YourByteRead(ByteRead), .CmdIsRead(CmdIsRead),
    .CorrectByteRead(CorrectByteRead), .Correct(Correct));
  Counter #(.width(10), .max('h3ff)) u_CorrectCounter (
    .count(and_3_out), .Q(CorrectCounter), .clk(CLK));  // open: load, D, carry, clr
  Counter #(.width(10), .max('h3ff)) u_HitCounter (
    .count(and_4_out), .Q(HitCounter), .clk(CLK));  // open: load, D, carry, clr
  Counter #(.width(10), .max('h3ff)) u_MissCounter (
    .count(and_5_out), .Q(MissCounter), .clk(CLK));  // open: load, D, carry, clr
  // Probe on CorrectCounter
  // Probe on HitCounter
  // Probe on MissCounter

  // Other names for the same wires on the sheet: DoneTesting = Halt

  // Notes on the sheet:
  //   Your Answer Inside Here
  //   Owner: Sean Malloy
  //   Partner: Aaron Kaloti
endmodule

module Cache (
  input  [9:0] CpuAddress,
  input  CpuRead,
  input  CpuWrite,
  input  [7:0] CpuWriteValue,
  input  CLK,
  input  [31:0] LineFromMem,
  output Ready,
  output DidContain,
  output [7:0] ByteRead,
  output [7:0] MemAddress,
  output MemRead,
  output MemWrite,
  output [31:0] Line2Mem
);

  wire and_1_out, CpuRead_t, CpuWrite_t, DidContain1, DidContain2, Dirty, Dirty1, Dirty2, Initialize,
       IsDirty, IsDirty1, IsDirty2, MemRead_t, or_1_out, ReturnData, ReturnData1, ReturnData2, S1, S1P, S2,
       S2P, S3, S3P, UpdateAges, UpdateAges1, UpdateAges2, UpdateDirty, UpdateDirty1, UpdateDirty2,
       UpdateOffs, UpdateOffs1, UpdateOffs2, UpdateVals1, UpdateVals2, WriteToMemBit, WriteToMemBit1,
       WriteToMemBit2;
  wire [1:0] CPU_Addr_q;
  wire [7:0] ByteRead1, ByteRead2, multiplexer_5_out, multiplexer_6_out, ReadInAddr, WriteVal1, WriteVal2;
  wire [7:1] Write2Addr1, Write2Addr2;
  wire [8:0] Tag1, Tag2;
  wire [31:0] Line2Mem1, Line2Mem2, LineFromMem1, LineFromMem2;

  Register #(.width(1)) CPU_Read (.D(CpuRead), .en(Ready), .Q(CpuRead_t), .clk(CLK));  // open: clr
  Register #(.width(1)) CPU_Write (.D(CpuWrite), .en(Ready), .Q(CpuWrite_t), .clk(CLK));  // open: clr
  or or_1 (or_1_out, CpuRead_t, CpuWrite_t);
  and and_1 (and_1_out, or_1_out, Ready);
  Demultiplexer #(.enable("false")) demultiplexer_1 (
    .out0(UpdateVals1), .out1(UpdateVals2), .in(MemRead), .sel(ReadInAddr[0]));
  Demultiplexer #(.enable("false")) demultiplexer_2 (
    .out0(UpdateOffs1), .out1(UpdateOffs2), .in(UpdateOffs), .sel(ReadInAddr[0]));
  Register #(.width(10)) CPU_Addr (
    .D(CpuAddress), .en(and_1_out), .Q({ReadInAddr, CPU_Addr_q}), .clk(CLK));  // open: clr
  Demultiplexer #(.width(9), .enable("false")) demultiplexer_3 (
    .out0(Tag1), .out1(Tag2), .in({ReadInAddr[7:1], CPU_Addr_q}), .sel(ReadInAddr[0]));
  Demultiplexer #(.width(8), .enable("false")) demultiplexer_4 (
    .out0(WriteVal1), .out1(WriteVal2), .in(CpuWriteValue), .sel(ReadInAddr[0]));
  Demultiplexer #(.enable("false")) demultiplexer_5 (
    .out0(WriteToMemBit1), .out1(WriteToMemBit2), .in(WriteToMemBit), .sel(ReadInAddr[0]));
  Demultiplexer #(.enable("false")) demultiplexer_6 (.out0(Dirty1), .out1(Dirty2), .in(Dirty), .sel(ReadInAddr[0]));
  Demultiplexer #(.enable("false")) demultiplexer_7 (
    .out0(ReturnData1), .out1(ReturnData2), .in(ReturnData), .sel(ReadInAddr[0]));
  Demultiplexer #(.enable("false")) demultiplexer_8 (
    .out0(UpdateAges1), .out1(UpdateAges2), .in(UpdateAges), .sel(ReadInAddr[0]));
  Demultiplexer #(.width(32), .enable("false")) demultiplexer_9 (
    .out0(LineFromMem1), .out1(LineFromMem2), .in(LineFromMem), .sel(ReadInAddr[0]));
  Demultiplexer #(.enable("false")) demultiplexer_10 (
    .out0(UpdateDirty1), .out1(UpdateDirty2), .in(UpdateDirty), .sel(ReadInAddr[0]));
  Sets sets_1 (
    .Tag_And_Offset(Tag1), .UpdateVals(UpdateVals1), .Clock(CLK), .UpdateOff(UpdateOffs1),
    .ReturnData(ReturnData1), .Write_Val(WriteVal1), .Update_Age(UpdateAges1), .Initialize(Initialize),
    .Line_From_Mem(LineFromMem1), .Write2Membit(WriteToMemBit1), .UpdateDirty(UpdateDirty1), .Dirty(Dirty1),
    .Read(CpuRead_t), .Write(CpuWrite_t), .Ready(Ready), .State({S3, S2, S1}), .IsDirty(IsDirty1),
    .byteRead(ByteRead1), .DidContain(DidContain1), .Line2Mem(Line2Mem1), .Tag(Write2Addr1));
  Sets sets_2 (
    .Tag_And_Offset(Tag2), .UpdateVals(UpdateVals2), .Clock(CLK), .UpdateOff(UpdateOffs2),
    .ReturnData(ReturnData2), .Write_Val(WriteVal2), .Update_Age(UpdateAges2), .Initialize(Initialize),
    .Line_From_Mem(LineFromMem2), .Write2Membit(WriteToMemBit2), .UpdateDirty(UpdateDirty2), .Dirty(Dirty2),
    .Read(CpuRead_t), .Write(CpuWrite_t), .Ready(Ready), .State({S3, S2, S1}), .IsDirty(IsDirty2),
    .byteRead(ByteRead2), .DidContain(DidContain2), .Line2Mem(Line2Mem2), .Tag(Write2Addr2));
  Controller controller_1 (
    .Read(CpuRead_t), .Write(CpuWrite_t), .DidContain(DidContain), .Dirty(IsDirty), .S2(S1), .S1(S2),
    .S0(S3), .UpdateAge(UpdateAges), .UpdateVals(MemRead), .UpdateOff(UpdateOffs), .DirtyP(Dirty),
    .MemRead(MemRead_t), .MemWrite(MemWrite), .ReadyP(Ready), .Initialize(Initialize), .S2P(S1P), .S1P(S2P),
    .S0P(S3P), .UpdateDirty(UpdateDirty));
  Register #(.width(3)) FSM (.D({S3P, S2P, S1P}), .Q({S3, S2, S1}), .clk(CLK));  // open: en, clr
  Multiplexer #(.enable("false")) multiplexer_1 (.in0(IsDirty1), .in1(IsDirty2), .out(IsDirty), .sel(ReadInAddr[0]));
  Multiplexer #(.width(8), .enable("false")) multiplexer_2 (
    .in0(ByteRead1), .in1(ByteRead2), .out(ByteRead), .sel(ReadInAddr[0]));
  Multiplexer #(.width(32), .enable("false")) multiplexer_3 (
    .in0(Line2Mem1), .in1(Line2Mem2), .out(Line2Mem), .sel(ReadInAddr[0]));
  Multiplexer #(.enable("false")) multiplexer_4 (
    .in0(DidContain1), .in1(DidContain2), .out(DidContain), .sel(ReadInAddr[0]));
  Multiplexer #(.width(8), .enable("false")) multiplexer_5 (
    .in0({Write2Addr1, ReadInAddr[0]}), .in1({Write2Addr2, ReadInAddr[0]}), .out(multiplexer_5_out),
    .sel(ReadInAddr[0]));
  Multiplexer #(.width(8), .enable("false")) multiplexer_6 (
    .in1(ReadInAddr), .out(multiplexer_6_out), .sel(MemRead_t));  // open: in0
  Multiplexer #(.width(8), .enable("false")) multiplexer_7 (
    .in0(multiplexer_6_out), .in1(multiplexer_5_out), .out(MemAddress), .sel(MemWrite));

  // Other names for the same wires on the sheet: State[2:0] = {S3, S2, S1}; MemAddr[7:0] = MemAddress;
  //   readRead = CpuRead; UpdateVals = MemRead; SetBit = ReadInAddr[0]; Write2Addr1[0] = ReadInAddr[0];
  //   Write2Addr2[0] = ReadInAddr[0]; writeWrite = CpuWrite

  // Notes on the sheet:
  //   Address Bits = 10
  //   Line Size = 4
  //   W = 3
  //   Num Sets = 2
  //   C =4*3*2 = 24bytes
  //   Tag bits = 7
endmodule

module Inputs (
  input  HaltTesting,
  input  Ready,
  input  CLK,
  output Done,
  output Read,
  output Write,
  output [9:0] Address,
  output [7:0] Value,
  output [9:0] TestNumber
);

  wire and_1_out, not_1_out, not_2_out;

  not not_1 (not_1_out, HaltTesting);
  not not_2 (not_2_out, Done);
  Counter #(.width(10), .max('h3ff), .ongoal("stay")) u_TestNumber (
    .count(and_1_out), .Q(TestNumber), .clk(CLK));  // open: load, D, carry, clr
  and and_1 (and_1_out, not_1_out, Ready, not_2_out);
  ROM #(.addrWidth(10), .dataWidth(21)) rom_1 (
    .addr(TestNumber), .data({Done, Read, Write, Address, Value}));  // open: sel

  // Notes on the sheet:
  //   contents of rom_1 (hex, n*v repeats v):
  //   80882 83fe6 4306b 83e0e 43701 42275 8280f 80304 41bd8 84371 43f77 41d70 4250b 44733 8253d 440d8
  //   82691 440c9 83d7c 43558 446bf 83837 842c9 43e0f 4059d 41556 80166 833b0 43a89 83142 8361c 42e66
  //   43eb6 42c00 43a0e 8165c 84682 8092a 83907 41f89 817b0 40855 82056 425e8 43ff2 8039f 42bd7 82137
  //   4416b 40273 8324a 814e4 44570 41c0f 429da 82640 8069c 8099e 414d5 41004 81beb 84113 419b1 81add
  //   83f35 425ff 829cd 40250 82945 4366d 40cc2 444f8 80814 81156 8446d 42a82 42bae 82578 41135 405d0
  //   8304b 82b3a 40972 822ba 4443a 42337 82506 80bd3 80560 83552 83955 81434 43096 43da1 81aa2 80305
  //   428e6 428cc 808a2 40e80 845f0 4215d 82765 82e29 40be5 82b74 42715 417a2 41fab 8452f 81c0a 83325
  //   44624 80205 42dfc 41333 40958 81348 42736 41069 84510 44669 826dd 8067e 408e4 44680 444e8 832ad
  //   821f8 83509 82d46 81184 432cd 80b77 4005a 440e0 81ea0 43d73 42b8c 80624 41468 42699 415ed 80fc1 0
  //   100000
endmodule

module Checker (
  input  [9:0] TestNumber,
  input  [7:0] YourByteRead,
  output CmdIsRead,
  output [7:0] CorrectByteRead,
  output Correct
);

  wire comparator_1_eq;
  wire [9:0] subtractor_1_out;

  // Probe on TestNumber
  Subtractor #(.width(10)) subtractor_1 (.a(TestNumber), .b(10'h1), .out(subtractor_1_out));  // open: bin, bout
  ROM #(.addrWidth(10), .dataWidth(9)) rom_1 (
    .addr(subtractor_1_out), .data({CmdIsRead, CorrectByteRead}));  // open: sel
  Comparator #(.mode("unsigned")) comparator_1 (
    .a(YourByteRead), .b(CorrectByteRead), .eq(comparator_1_eq));  // open: gt, lt
  and and_1 (Correct, comparator_1_eq, CmdIsRead);

  // Other names for the same wires on the sheet: Test_Number[9:0] = TestNumber

  // Notes on the sheet:
  //   Read Solutions
  //   contents of rom_1 (hex, n*v repeats v):
  //   1a3 1dc 6b 125 1 75 1dc 1c3 d8 1ab 77 70 b 33 10b d8 1c3 c9 174 58 bf 153 199 f 9d 56 1bb 13b 89 16c
  //   180 66 b6 0 e 107 1bf 1d8 167 89 118 55 1a2 e8 f2 1c3 d7 142 6b 73 1ab 18c 70 f da 1c3 14c 1d8 d5 4
  //   1d8 16b b1 1f4 1f2 ff 1da 50 1da 6d c2 f8 155 1c6 1f8 82 ae 1ff 35 d0 16b 1ae 72 175 3a 37 1ff 173
  //   1d0 158 167 1d5 96 a1 1f4 1c3 e6 cc 155 80 170 5d 1e6 166 e5 1ae 15 a2 ab 170 10f 13b 24 150 fc 33
  //   58 133 36 69 170 69 1c3 14c e4 80 e8 1ab 15d 158 1fc 135 cd 1e5 5a e0 104 73 8c 14c 68 99 ed 1a6
endmodule

module Sets (
  input  [8:0] Tag_And_Offset,
  input  UpdateVals,
  input  Clock,
  input  UpdateOff,
  input  ReturnData,
  input  [7:0] Write_Val,
  input  Update_Age,
  input  Initialize,
  input  [31:0] Line_From_Mem,
  input  Write2Membit,
  input  UpdateDirty,
  input  Dirty,
  input  Read,
  input  Write,
  input  Ready,
  input  [2:0] State,
  output IsDirty,
  output [7:0] byteRead,
  output DidContain,
  output [31:0] Line2Mem,
  output [6:0] Tag
);

  wire Age_1reset, Age_2reset, Age_3reset, bitfinder_1_found, comparator_1_lt, comparator_2_lt,
       comparator_3_lt, comparator_4_eq, DidContain1, DidContain2, DidContain3, Dirty1, Dirty2, Dirty3;
  wire [1:0] adder_1_out, adder_2_out, adder_3_out, Age_1, Age_1P, Age_2, Age_2P, Age_3, Age_3P,
       bitfinder_1_index, multiplexer_1_out, multiplexer_2_out, multiplexer_5_out, multiplexer_10_out,
       multiplexer_11_out, Old_age, Oldest_age, Tag_Contained, undriven, undriven_2, undriven_3;
  wire [2:0] comparator_5_eq;
  wire [6:0] Tag1, Tag2, Tag3;
  wire [7:0] multiplexer_13_out, ValRead1, ValRead2, ValRead3, Write_Val1, Write_Val2, Write_Val3;
  wire [31:0] LineFromMem1, LineFromMem2, LineFromMem3, multiplexer_15_out, Write2Mem1, Write2Mem2,
       Write2Mem3;

  Comparator #(.width(2), .mode("unsigned")) comparator_1 (
    .a(Age_1), .b(Old_age), .lt(comparator_1_lt));  // open: gt, eq
  Comparator #(.width(2), .mode("unsigned")) comparator_2 (
    .a(Age_2), .b(Old_age), .lt(comparator_2_lt));  // open: gt, eq
  Comparator #(.width(2), .mode("unsigned")) comparator_3 (
    .a(Age_3), .b(Old_age), .lt(comparator_3_lt));  // open: gt, eq
  Multiplexer #(.width(2), .enable("false")) multiplexer_1 (
    .in0(Age_1), .in1(adder_1_out), .out(multiplexer_1_out), .sel(comparator_1_lt));
  Adder #(.width(2)) adder_1 (.a(Age_1), .b(2'b01), .out(adder_1_out));  // open: cin, cout
  Multiplexer #(.width(2), .enable("false")) multiplexer_2 (
    .in0(Age_2), .in1(adder_2_out), .out(multiplexer_2_out), .sel(comparator_2_lt));
  Adder #(.width(2)) adder_2 (.a(Age_2), .b(2'b01), .out(adder_2_out));  // open: cin, cout
  Adder #(.width(2)) adder_3 (.a(Age_3), .b(2'b01), .out(adder_3_out));  // open: cin, cout
  Multiplexer #(.width(2), .enable("false")) multiplexer_3 (
    .in0(multiplexer_1_out), .in1(2'b00), .out(Age_1P), .sel(Age_1reset));
  Multiplexer #(.width(2), .enable("false")) multiplexer_4 (
    .in0(multiplexer_2_out), .in1(2'b00), .out(Age_2P), .sel(Age_2reset));
  Multiplexer #(.width(2), .enable("false")) multiplexer_5 (
    .in0(Age_3), .in1(adder_3_out), .out(multiplexer_5_out), .sel(comparator_3_lt));
  Lines Line_1 (
    .Line_From_Mem(Line_From_Mem), .writeVal(Write_Val), .Dirty(Dirty), .UpdateDirty(UpdateDirty),
    .Offset(Tag_And_Offset[1:0]), .UpdateOff(UpdateOff), .UpdateVals(UpdateVals), .Tag(Tag_And_Offset[8:2]),
    .Clock(Clock), .Age(Age_1P), .Update_Age(Update_Age), .Write_to_mem_bit(Write2Membit),
    .ValRead(ValRead1), .isDirty(Dirty1), .Write_to_mem(Write2Mem1), .DidContain(DidContain1), .Tag_2(Tag1),
    .Age_2(Age_1));
  Lines Line_2 (
    .Line_From_Mem(Line_From_Mem), .writeVal(Write_Val), .Dirty(Dirty), .UpdateDirty(UpdateDirty),
    .Offset(Tag_And_Offset[1:0]), .UpdateOff(UpdateOff), .UpdateVals(UpdateVals), .Tag(Tag_And_Offset[8:2]),
    .Clock(Clock), .Age(Age_2P), .Update_Age(Update_Age), .Write_to_mem_bit(Write2Membit),
    .ValRead(ValRead2), .isDirty(Dirty2), .Write_to_mem(Write2Mem2), .DidContain(DidContain2), .Tag_2(Tag2),
    .Age_2(Age_2));
  Lines Line_3 (
    .Line_From_Mem(Line_From_Mem), .writeVal(Write_Val), .Dirty(Dirty), .UpdateDirty(UpdateDirty),
    .Offset(Tag_And_Offset[1:0]), .UpdateOff(UpdateOff), .UpdateVals(UpdateVals), .Tag(Tag_And_Offset[8:2]),
    .Clock(Clock), .Age(Age_3P), .Update_Age(Update_Age), .Write_to_mem_bit(Write2Membit),
    .ValRead(ValRead3), .isDirty(Dirty3), .Write_to_mem(Write2Mem3), .DidContain(DidContain3), .Tag_2(Tag3),
    .Age_2(Age_3));
  Multiplexer #(.width(2), .enable("false")) multiplexer_6 (
    .in0(multiplexer_5_out), .in1(2'b00), .out(Age_3P), .sel(Age_3reset));
  Multiplexer #(.width(2), .enable("false")) multiplexer_7 (.in0(Age_1), .in1(2'b10), .out(Age_1P), .sel(Initialize));
  Multiplexer #(.width(2), .enable("false")) multiplexer_8 (.in0(Age_2), .in1(2'b01), .out(Age_2P), .sel(Initialize));
  Multiplexer #(.width(2), .enable("false")) multiplexer_9 (.in0(Age_3), .in1(2'b00), .out(Age_3P), .sel(Initialize));
  Multiplexer #(.width(2), .enable("false")) multiplexer_10 (
    .in0(Old_age), .in1(Tag_Contained), .out(multiplexer_10_out), .sel(DidContain));
  Demultiplexer #(.select(2), .enable("false")) demultiplexer_1 (
    .out0(Age_1reset), .out1(Age_2reset), .out2(Age_3reset), .in(1'b1), .sel(multiplexer_10_out));  // open: out3
  Demultiplexer #(.width(2), .enable("false")) demultiplexer_2 (
    .out0(Oldest_age), .out1(Tag_Contained), .in(undriven), .sel(DidContain));
  Multiplexer #(.select(2), .width(2), .enable("false")) multiplexer_11 (
    .in0(Age_1), .in1(Age_2), .in2(Age_3), .out(multiplexer_11_out), .sel(undriven));  // open: in3
  Register #(.width(2)) u_Old_age (.D(multiplexer_11_out), .en(Update_Age), .Q(Old_age), .clk(Clock), .clr(Ready));
  Multiplexer #(.select(2), .enable("false")) multiplexer_12 (
    .in0(Dirty1), .in1(Dirty2), .in2(Dirty3), .out(IsDirty), .sel(Tag_Contained));  // open: in3
  Comparator #(.width(3), .mode("unsigned")) comparator_4 (
    .a(State), .b(3'b010), .eq(comparator_4_eq));  // open: gt, lt
  BitFinder #(.width(3)) bitfinder_1 (
    .in({DidContain3, DidContain2, DidContain1}), .index(bitfinder_1_index), .found(bitfinder_1_found));
  Multiplexer #(.width(8), .enable("false")) multiplexer_13 (
    .in1(Write_Val), .out(multiplexer_13_out), .sel(UpdateOff));  // open: in0
  Demultiplexer #(.select(2), .width(8), .enable("false")) demultiplexer_3 (
    .out0(Write_Val1), .out1(Write_Val2), .out2(Write_Val3), .in(multiplexer_13_out), .sel(Tag_Contained));  // open: out3
  Register #(.width(2)) TagContain (
    .D(bitfinder_1_index), .en(comparator_4_eq), .Q(Tag_Contained), .clk(Clock));  // open: clr
  Register #(.width(1)) u_DidContain (
    .D(bitfinder_1_found), .en(comparator_4_eq), .Q(DidContain), .clk(Clock));  // open: clr
  Demultiplexer #(.select(2), .width(32), .enable("false")) demultiplexer_4 (
    .out0(LineFromMem1), .out1(LineFromMem2), .out2(LineFromMem3), .in(Line_From_Mem), .sel(Old_age));  // open: out3
  Comparator #(.width(2), .mode("unsigned")) comparator_5 (
    .a(Age_1), .b(2'b10), .eq(comparator_5_eq[0]));  // open: gt, lt
  Comparator #(.width(2), .mode("unsigned")) comparator_6 (
    .a(Age_2), .b(2'b10), .eq(comparator_5_eq[1]));  // open: gt, lt
  Comparator #(.width(2), .mode("unsigned")) comparator_7 (
    .a(Age_3), .b(2'b10), .eq(comparator_5_eq[2]));  // open: gt, lt
  Demultiplexer #(.width(2), .enable("false")) demultiplexer_5 (
    .out0(Old_age), .out1(Tag_Contained), .in(undriven_2), .sel(DidContain));
  Multiplexer #(.select(2), .width(8), .enable("false")) multiplexer_14 (
    .in0(ValRead1), .in1(ValRead2), .in2(ValRead3), .out(byteRead), .sel(undriven_2));  // open: in3
  Multiplexer #(.select(2), .width(32), .enable("false")) multiplexer_15 (
    .in0(Write2Mem1), .in1(Write2Mem2), .in2(Write2Mem3), .out(multiplexer_15_out), .sel(Old_age));  // open: in3
  BitFinder #(.width(3)) bitfinder_2 (.in(comparator_5_eq), .index(Oldest_age));  // open: found
  Demultiplexer #(.width(2), .enable("false")) demultiplexer_6 (
    .out0(Old_age), .out1(Tag_Contained), .in(undriven_3), .sel(DidContain));
  Multiplexer #(.width(32), .enable("false")) multiplexer_16 (
    .in1(multiplexer_15_out), .out(Line2Mem), .sel(Write2Membit));  // open: in0
  Multiplexer #(.select(2), .width(7), .enable("false")) multiplexer_17 (
    .in0(Tag1), .in1(Tag2), .in2(Tag3), .out(Tag), .sel(undriven_3));  // open: in3

  // Other names for the same wires on the sheet: Clk = Clock; LineFromMem[31:0] = Line_From_Mem;
  //   Offset[1:0] = Tag_And_Offset[1:0]; Tag_t[6:0] = Tag_And_Offset[8:2]
endmodule

module Lines (
  input  [31:0] Line_From_Mem,
  input  [7:0] writeVal,
  input  Dirty,
  input  UpdateDirty,
  input  [1:0] Offset,
  input  UpdateOff,
  input  UpdateVals,
  input  [6:0] Tag,
  input  Clock,
  input  [1:0] Age,
  input  Update_Age,
  input  Write_to_mem_bit,
  output [7:0] ValRead,
  output isDirty,
  output [31:0] Write_to_mem,
  output DidContain,
  output [6:0] Tag_2,
  output [1:0] Age_2
);

  wire and_2_out, and_3_out, and_4_out, and_5_out, comparator_1_eq, comparator_2_eq, comparator_3_eq,
       comparator_4_eq, comparator_5_eq, or_1_out, Valid_q;
  wire [7:0] demultiplexer_1_out0, demultiplexer_1_out1, demultiplexer_1_out2, demultiplexer_1_out3, Val1,
       Val1P, Val2, Val2P, Val3, Val3P, Val4, Val4P;

  or or_1 (or_1_out, UpdateOff, UpdateVals);
  Register #(.width(2)) u_Age (.D(Age), .en(Update_Age), .Q(Age_2), .clk(Clock));  // open: clr
  Register Val0 (.D(Val1P), .en(or_1_out), .Q(Val1), .clk(Clock));  // open: clr
  Register u_Val1 (.D(Val2P), .en(or_1_out), .Q(Val2), .clk(Clock));  // open: clr
  Register u_Val2 (.D(Val3P), .en(or_1_out), .Q(Val3), .clk(Clock));  // open: clr
  Register u_Val3 (.D(Val4P), .en(or_1_out), .Q(Val4), .clk(Clock));  // open: clr
  Register #(.width(1)) u_Dirty (.D(Dirty), .en(UpdateDirty), .Q(isDirty), .clk(Clock));  // open: clr
  Register #(.width(1)) Valid (.D(1'b1), .en(UpdateVals), .Q(Valid_q), .clk(Clock));  // open: clr
  Register #(.width(7)) u_Tag (.D(Tag), .en(UpdateVals), .Q(Tag_2), .clk(Clock));  // open: clr
  Demultiplexer #(.select(2), .width(8), .enable("false")) demultiplexer_1 (
    .out0(demultiplexer_1_out0), .out1(demultiplexer_1_out1), .out2(demultiplexer_1_out2),
    .out3(demultiplexer_1_out3), .in(writeVal), .sel(Offset));
  Comparator #(.width(7), .mode("unsigned")) comparator_1 (.a(Tag_2), .b(Tag), .eq(comparator_1_eq));  // open: gt, lt
  Multiplexer #(.width(8), .enable("false")) multiplexer_1 (
    .in0(Val1), .in1(Line_From_Mem[7:0]), .out(Val1P), .sel(UpdateVals));
  Multiplexer #(.width(8), .enable("false")) multiplexer_2 (
    .in0(Val2), .in1(Line_From_Mem[15:8]), .out(Val2P), .sel(UpdateVals));
  Multiplexer #(.width(8), .enable("false")) multiplexer_3 (
    .in0(Val3), .in1(Line_From_Mem[23:16]), .out(Val3P), .sel(UpdateVals));
  Multiplexer #(.width(8), .enable("false")) multiplexer_4 (
    .in0(Val4), .in1(Line_From_Mem[31:24]), .out(Val4P), .sel(UpdateVals));
  and and_1 (DidContain, Valid_q, comparator_1_eq);
  Multiplexer #(.width(8), .enable("false")) multiplexer_5 (
    .in0(Val1), .in1(demultiplexer_1_out0), .out(Val1P), .sel(and_2_out));
  Multiplexer #(.width(8), .enable("false")) multiplexer_6 (
    .in0(Val2), .in1(demultiplexer_1_out1), .out(Val2P), .sel(and_3_out));
  Multiplexer #(.width(8), .enable("false")) multiplexer_7 (
    .in0(Val3), .in1(demultiplexer_1_out2), .out(Val3P), .sel(and_4_out));
  Multiplexer #(.width(8), .enable("false")) multiplexer_8 (
    .in0(Val4), .in1(demultiplexer_1_out3), .out(Val4P), .sel(and_5_out));
  Demultiplexer #(.select(2), .width(8), .enable("false")) demultiplexer_2 (
    .out0(Val1), .out1(Val2), .out2(Val3), .out3(Val4), .in(ValRead), .sel(Offset));
  and and_2 (and_2_out, UpdateOff, comparator_2_eq);
  and and_3 (and_3_out, UpdateOff, comparator_3_eq);
  and and_4 (and_4_out, UpdateOff, comparator_4_eq);
  and and_5 (and_5_out, UpdateOff, comparator_5_eq);
  Multiplexer #(.width(32), .enable("false")) multiplexer_9 (
    .in1({Val4, Val3, Val2, Val1}), .out(Write_to_mem), .sel(Write_to_mem_bit));  // open: in0
  Comparator #(.width(2), .mode("unsigned")) comparator_2 (
    .a(Offset), .b(2'b00), .eq(comparator_2_eq));  // open: gt, lt
  Comparator #(.width(2), .mode("unsigned")) comparator_3 (
    .a(Offset), .b(2'b01), .eq(comparator_3_eq));  // open: gt, lt
  Comparator #(.width(2), .mode("unsigned")) comparator_4 (
    .a(Offset), .b(2'b10), .eq(comparator_4_eq));  // open: gt, lt
  Comparator #(.width(2), .mode("unsigned")) comparator_5 (
    .a(Offset), .b(2'b11), .eq(comparator_5_eq));  // open: gt, lt

  // Other names for the same wires on the sheet: clk = Clock; LineFromMem[31:0] = Line_From_Mem;
  //   memWrite = Write_to_mem_bit
endmodule

module Controller (
  input  Read,
  input  Write,
  input  DidContain,
  input  Dirty,
  input  S2,
  input  S1,
  input  S0,
  output UpdateAge,
  output UpdateVals,
  output UpdateOff,
  output DirtyP,
  output MemRead,
  output MemWrite,
  output ReadyP,
  output Initialize,
  output S2P,
  output S1P,
  output S0P,
  output UpdateDirty
);

  wire and_1_out, and_2_out, and_3_out, and_4_out, and_5_out, and_6_out, and_7_out, and_8_out, and_9_out,
       and_10_out, and_11_out, and_12_out, and_13_out, and_14_out, and_15_out, and_16_out, and_17_out,
       and_18_out, and_19_out, and_20_out, and_21_out, and_22_out, and_23_out, and_24_out, and_25_out,
       and_26_out, and_27_out, and_28_out, and_29_out, and_30_out, and_31_out, and_32_out, and_33_out,
       and_34_out, and_35_out, and_36_out, and_37_out, and_38_out, and_39_out, and_40_out, and_41_out,
       and_42_out, and_43_out, and_44_out, and_45_out, and_46_out, and_47_out, and_48_out, and_49_out,
       and_50_out, and_51_out, and_52_out, and_53_out, not_1_out, not_2_out, not_3_out, not_4_out, not_5_out,
       not_6_out, not_7_out, not_8_out, not_9_out, not_10_out, not_11_out, not_12_out, not_13_out,
       not_14_out, not_15_out, not_16_out, not_17_out, not_18_out, not_19_out, not_20_out, not_21_out,
       not_22_out, not_23_out, not_24_out, not_25_out, not_26_out, not_27_out, not_28_out, not_29_out,
       not_30_out, not_31_out, not_32_out, not_33_out, not_34_out, not_35_out, not_36_out, not_37_out,
       not_38_out, not_39_out, not_40_out, not_41_out, not_42_out, not_43_out, not_44_out, not_45_out,
       not_46_out, not_47_out, not_48_out, not_49_out, not_50_out, not_51_out, not_52_out, not_53_out,
       not_54_out, not_55_out, not_56_out, not_57_out, not_58_out, not_59_out, not_60_out, not_61_out,
       not_62_out, not_63_out, not_64_out, not_65_out, not_66_out, not_67_out, not_68_out, not_69_out,
       not_70_out, not_71_out, not_72_out, not_73_out, not_74_out, not_75_out, not_76_out, not_77_out,
       not_78_out, not_79_out, not_80_out, not_81_out, not_82_out, not_83_out, not_84_out, not_85_out,
       not_86_out, not_87_out, not_88_out, not_89_out, not_90_out, not_91_out, not_92_out, not_93_out,
       not_94_out, not_95_out, not_96_out, not_97_out, not_98_out, not_99_out, not_100_out, not_101_out,
       not_102_out, not_103_out, not_104_out, not_105_out, not_106_out, not_107_out, not_108_out,
       not_109_out, not_110_out, not_111_out, not_112_out, not_113_out, not_114_out, not_115_out,
       not_116_out, not_117_out, not_118_out, not_119_out, not_120_out, not_121_out, not_122_out,
       not_123_out, not_124_out, not_125_out, not_126_out, not_127_out, not_128_out, not_129_out,
       not_130_out, not_131_out, not_132_out, not_133_out, not_134_out, not_135_out, not_136_out,
       not_137_out, not_138_out, not_139_out, not_140_out, not_141_out, not_142_out, not_143_out,
       not_144_out, not_145_out, not_146_out, not_147_out, not_148_out, not_149_out, not_150_out,
       not_151_out, not_152_out, not_153_out, not_154_out, not_155_out, not_156_out, not_157_out,
       not_158_out, not_159_out;

  not not_1 (not_1_out, Write);
  not not_2 (not_2_out, S2);
  not not_3 (not_3_out, S1);
  not not_4 (not_4_out, S0);
  not not_5 (not_5_out, Read);
  not not_6 (not_6_out, S2);
  not not_7 (not_7_out, S1);
  not not_8 (not_8_out, Write);
  not not_9 (not_9_out, S2);
  not not_10 (not_10_out, S1);
  not not_11 (not_11_out, Read);
  not not_12 (not_12_out, DidContain);
  not not_13 (not_13_out, Dirty);
  not not_14 (not_14_out, S2);
  not not_15 (not_15_out, Read);
  not not_16 (not_16_out, DidContain);
  not not_17 (not_17_out, S1);
  not not_18 (not_18_out, S0);
  not not_19 (not_19_out, Write);
  not not_20 (not_20_out, DidContain);
  not not_21 (not_21_out, Dirty);
  not not_22 (not_22_out, S2);
  not not_23 (not_23_out, Write);
  not not_24 (not_24_out, DidContain);
  not not_25 (not_25_out, S1);
  not not_26 (not_26_out, S0);
  not not_27 (not_27_out, Read);
  not not_28 (not_28_out, DidContain);
  not not_29 (not_29_out, S1);
  not not_30 (not_30_out, Read);
  not not_31 (not_31_out, S2);
  not not_32 (not_32_out, Write);
  not not_33 (not_33_out, S2);
  not not_34 (not_34_out, S1);
  not not_35 (not_35_out, S0);
  not not_36 (not_36_out, Read);
  not not_37 (not_37_out, DidContain);
  not not_38 (not_38_out, S1);
  not not_39 (not_39_out, Write);
  not not_40 (not_40_out, DidContain);
  not not_41 (not_41_out, S1);
  not not_42 (not_42_out, Read);
  not not_43 (not_43_out, DidContain);
  not not_44 (not_44_out, Dirty);
  not not_45 (not_45_out, S2);
  not not_46 (not_46_out, Read);
  not not_47 (not_47_out, DidContain);
  not not_48 (not_48_out, S1);
  not not_49 (not_49_out, S0);
  not not_50 (not_50_out, Write);
  not not_51 (not_51_out, DidContain);
  not not_52 (not_52_out, Dirty);
  not not_53 (not_53_out, S2);
  not not_54 (not_54_out, Write);
  not not_55 (not_55_out, DidContain);
  not not_56 (not_56_out, S1);
  not not_57 (not_57_out, S0);
  not not_58 (not_58_out, Read);
  not not_59 (not_59_out, DidContain);
  not not_60 (not_60_out, S2);
  not not_61 (not_61_out, Write);
  not not_62 (not_62_out, DidContain);
  not not_63 (not_63_out, S2);
  not not_64 (not_64_out, Read);
  not not_65 (not_65_out, Write);
  not not_66 (not_66_out, Read);
  not not_67 (not_67_out, Write);
  not not_68 (not_68_out, Read);
  not not_69 (not_69_out, Write);
  not not_70 (not_70_out, Write);
  not not_71 (not_71_out, Dirty);
  not not_72 (not_72_out, Write);
  not not_73 (not_73_out, Write);
  not not_74 (not_74_out, Read);
  not not_75 (not_75_out, S2);
  not not_76 (not_76_out, S1);
  not not_77 (not_77_out, S0);
  not not_78 (not_78_out, Write);
  not not_79 (not_79_out, S2);
  not not_80 (not_80_out, S1);
  not not_81 (not_81_out, S0);
  not not_82 (not_82_out, Read);
  not not_83 (not_83_out, DidContain);
  not not_84 (not_84_out, S2);
  not not_85 (not_85_out, Read);
  not not_86 (not_86_out, DidContain);
  not not_87 (not_87_out, S1);
  not not_88 (not_88_out, S0);
  not not_89 (not_89_out, Read);
  not not_90 (not_90_out, S2);
  not not_91 (not_91_out, S0);
  not not_92 (not_92_out, Write);
  not not_93 (not_93_out, DidContain);
  not not_94 (not_94_out, S2);
  not not_95 (not_95_out, Write);
  not not_96 (not_96_out, DidContain);
  not not_97 (not_97_out, S1);
  not not_98 (not_98_out, S0);
  not not_99 (not_99_out, Read);
  not not_100 (not_100_out, S2);
  not not_101 (not_101_out, S1);
  not not_102 (not_102_out, Read);
  not not_103 (not_103_out, DidContain);
  not not_104 (not_104_out, S2);
  not not_105 (not_105_out, S0);
  not not_106 (not_106_out, Write);
  not not_107 (not_107_out, S2);
  not not_108 (not_108_out, S1);
  not not_109 (not_109_out, Write);
  not not_110 (not_110_out, DidContain);
  not not_111 (not_111_out, S2);
  not not_112 (not_112_out, S0);
  not not_113 (not_113_out, Write);
  not not_114 (not_114_out, S2);
  not not_115 (not_115_out, S1);
  not not_116 (not_116_out, S0);
  not not_117 (not_117_out, Read);
  not not_118 (not_118_out, DidContain);
  not not_119 (not_119_out, S1);
  not not_120 (not_120_out, S0);
  not not_121 (not_121_out, Read);
  not not_122 (not_122_out, S2);
  not not_123 (not_123_out, S0);
  not not_124 (not_124_out, Read);
  not not_125 (not_125_out, Dirty);
  not not_126 (not_126_out, S2);
  not not_127 (not_127_out, Read);
  not not_128 (not_128_out, DidContain);
  not not_129 (not_129_out, S1);
  not not_130 (not_130_out, Read);
  not not_131 (not_131_out, S2);
  not not_132 (not_132_out, Write);
  not not_133 (not_133_out, DidContain);
  not not_134 (not_134_out, S1);
  not not_135 (not_135_out, S0);
  not not_136 (not_136_out, Write);
  not not_137 (not_137_out, S2);
  not not_138 (not_138_out, S0);
  not not_139 (not_139_out, Write);
  not not_140 (not_140_out, DidContain);
  not not_141 (not_141_out, Dirty);
  not not_142 (not_142_out, S2);
  not not_143 (not_143_out, Write);
  not not_144 (not_144_out, DidContain);
  not not_145 (not_145_out, S1);
  not not_146 (not_146_out, Read);
  not not_147 (not_147_out, DidContain);
  not not_148 (not_148_out, S1);
  not not_149 (not_149_out, Read);
  not not_150 (not_150_out, S2);
  not not_151 (not_151_out, Write);
  not not_152 (not_152_out, DidContain);
  not not_153 (not_153_out, Dirty);
  not not_154 (not_154_out, S2);
  not not_155 (not_155_out, Write);
  not not_156 (not_156_out, DidContain);
  not not_157 (not_157_out, S1);
  and and_1 (and_1_out, not_1_out, not_2_out, not_3_out, not_4_out);
  and and_2 (and_2_out, not_5_out, Write, not_6_out, not_7_out);
  and and_3 (and_3_out, Read, not_8_out, not_9_out, not_10_out);
  and and_4 (and_4_out, not_11_out, Write, not_12_out, not_13_out, not_14_out, S1, S0);
  and and_5 (and_5_out, not_15_out, Write, not_16_out, Dirty, S2, not_17_out, not_18_out);
  and and_6 (and_6_out, Read, not_19_out, not_20_out, not_21_out, not_22_out, S1, S0);
  and and_7 (and_7_out, Read, not_23_out, not_24_out, Dirty, S2, not_25_out, not_26_out);
  and and_8 (and_8_out, not_27_out, Write, not_28_out, S2, not_29_out, S0);
  and and_9 (and_9_out, not_30_out, Write, DidContain, not_31_out, S1, S0);
  and and_10 (and_10_out, not_32_out, not_33_out, not_34_out, not_35_out);
  and and_11 (and_11_out, not_36_out, Write, not_37_out, not_38_out);
  not not_158 (not_158_out, Read);
  and and_12 (and_12_out, not_158_out, Write, not_159_out);
  not not_159 (not_159_out, S2);
  and and_13 (and_13_out, Read, not_39_out, not_40_out, Dirty, S2, not_41_out, S0);
  and and_14 (and_14_out, not_42_out, Write, not_43_out, not_44_out, not_45_out, S1, S0);
  and and_15 (and_15_out, not_46_out, Write, not_47_out, Dirty, S2, not_48_out, not_49_out);
  and and_16 (and_16_out, Read, not_50_out, not_51_out, not_52_out, not_53_out, S1, S0);
  and and_17 (and_17_out, Read, not_54_out, not_55_out, Dirty, S2, not_56_out, not_57_out);
  and and_18 (and_18_out, not_58_out, Write, not_59_out, Dirty, not_60_out, S1, S0);
  and and_19 (and_19_out, Read, not_61_out, not_62_out, Dirty, not_63_out, S1, S0);
  and and_20 (and_20_out, not_64_out, not_65_out, S0);
  and and_21 (and_21_out, not_66_out, not_67_out, S1);
  and and_22 (and_22_out, not_68_out, not_69_out, S2);
  and and_23 (and_23_out, not_70_out, not_71_out, S2);
  and and_24 (and_24_out, S2, S0);
  and and_25 (and_25_out, S2, S1);
  and and_26 (and_26_out, not_72_out, DidContain, S1);
  and and_27 (and_27_out, not_73_out, DidContain, S2);
  and and_28 (and_28_out, Read, Write);
  and and_29 (and_29_out, not_74_out, not_75_out, not_76_out, not_77_out);
  and and_30 (and_30_out, not_78_out, not_79_out, not_80_out, not_81_out);
  and and_31 (and_31_out, not_82_out, Write, not_83_out, not_84_out, S1, S0);
  and and_32 (and_32_out, not_85_out, Write, not_86_out, Dirty, S2, not_87_out, not_88_out);
  and and_33 (and_33_out, not_89_out, Write, DidContain, not_90_out, S1, not_91_out);
  and and_34 (and_34_out, Read, not_92_out, not_93_out, not_94_out, S1, S0);
  and and_35 (and_35_out, Read, not_95_out, not_96_out, Dirty, S2, not_97_out, not_98_out);
  and and_36 (and_36_out, not_99_out, Write, not_100_out, not_101_out, S0);
  and and_37 (and_37_out, not_102_out, Write, not_103_out, not_104_out, S1, not_105_out);
  and and_38 (and_38_out, Read, not_106_out, not_107_out, not_108_out, S0);
  and and_39 (and_39_out, Read, not_109_out, not_110_out, not_111_out, S1, not_112_out);
  and and_40 (and_40_out, not_113_out, not_114_out, not_115_out, not_116_out);
  and and_41 (and_41_out, not_117_out, Write, not_118_out, not_119_out, not_120_out);
  and and_42 (and_42_out, not_121_out, Write, not_122_out, not_123_out);
  and and_43 (and_43_out, not_124_out, Write, not_125_out, not_126_out, S1);
  and and_44 (and_44_out, not_127_out, Write, not_128_out, Dirty, S2, not_129_out);
  and and_45 (and_45_out, not_130_out, Write, DidContain, not_131_out, S1);
  and and_46 (and_46_out, Read, not_132_out, not_133_out, not_134_out, not_135_out);
  and and_47 (and_47_out, Read, not_136_out, not_137_out, not_138_out);
  and and_48 (and_48_out, Read, not_139_out, not_140_out, not_141_out, not_142_out, S1);
  and and_49 (and_49_out, Read, not_143_out, not_144_out, Dirty, S2, not_145_out);
  and and_50 (and_50_out, not_146_out, Write, not_147_out, S2, not_148_out, S0);
  and and_51 (and_51_out, not_149_out, Write, DidContain, not_150_out, S1, S0);
  and and_52 (and_52_out, Read, not_151_out, not_152_out, not_153_out, not_154_out, S1, S0);
  and and_53 (and_53_out, Read, not_155_out, not_156_out, Dirty, S2, not_157_out, S0);
  or or_1 (UpdateAge, and_1_out, and_2_out, and_3_out);
  or or_2 (UpdateVals, and_4_out, and_5_out, and_6_out, and_7_out);
  or or_3 (UpdateOff, and_8_out, and_9_out);
  or or_4 (DirtyP, and_10_out, and_11_out, and_12_out, and_13_out);
  or or_5 (MemRead, and_14_out, and_15_out, and_16_out, and_17_out);
  or or_6 (MemWrite, and_18_out, and_19_out);
  or or_7 (ReadyP, and_20_out, and_21_out, and_22_out, and_23_out, and_24_out, and_25_out, and_26_out, and_27_out, and_28_out);
  or or_8 (Initialize, and_29_out, and_30_out);
  or or_9 (S2P, and_31_out, and_32_out, and_33_out, and_34_out, and_35_out);
  or or_10 (S1P, and_36_out, and_37_out, and_38_out, and_39_out);
  or or_11 (UpdateDirty, and_50_out, and_51_out, and_52_out, and_53_out);
  or or_12 (S0P, and_40_out, and_41_out, and_42_out, and_43_out, and_44_out, and_45_out, and_46_out, and_47_out, and_48_out, and_49_out);
endmodule
