// Logisim project CPU.circ as structural Verilog
module CPU (
);

  wire CLK;
  wire [4:0] PC_q;
  wire [15:0] rom_1_data;

  Clock clock_1 (.out(CLK));
  Register #(.width(5)) PC (.Q(PC_q));  // open: D, en, clk, clr
  ROM #(.addrWidth(5), .dataWidth(16)) rom_1 (.addr(PC_q), .data(rom_1_data));  // open: sel
  decoder decoder ();
  Reg_File Reg_File (.CLK(CLK));  // open: A, B, C, Data_In, Reg_Write, A_DATA, B_DATA

  // Notes on the sheet:
  //   Instructions
  //   contents of rom_1 (hex, n*v repeats v):
  //   2003 2106 1005 3210 4301 5433 6520 763c 8720 986f b938 ca77 db13 ec62 fd85 e05
endmodule

module Reg_File (
  input  [3:0] A,
  input  [3:0] B,
  input  [3:0] C,
  input  [3:0] Data_In,
  input  Reg_Write,
  input  CLK,
  output [3:0] A_DATA,
  output [3:0] B_DATA
);

  wire Write_Reg0, Write_Reg1, Write_Reg2, Write_Reg3, Write_Reg4, Write_Reg5, Write_Reg6, Write_Reg7,
       Write_Reg8, Write_Reg9, Write_Reg10, Write_Reg11, Write_Reg12, Write_Reg13, Write_Reg14, Write_Reg15;
  wire [3:0] Reg0, Reg1, Reg2, Reg3, Reg4, Reg5, Reg6, Reg7, Reg8, Reg9, Reg10, Reg11, Reg12, Reg13, Reg14,
       Reg15;

  Demultiplexer #(.select(4), .enable("false")) demultiplexer_1 (
    .out0(Write_Reg0), .out1(Write_Reg1), .out2(Write_Reg2), .out3(Write_Reg3), .out4(Write_Reg4),
    .out5(Write_Reg5), .out6(Write_Reg6), .out7(Write_Reg7), .out8(Write_Reg8), .out9(Write_Reg9),
    .out10(Write_Reg10), .out11(Write_Reg11), .out12(Write_Reg12), .out13(Write_Reg13), .out14(Write_Reg14),
    .out15(Write_Reg15), .in(Reg_Write), .sel(C));
  // Probe on Reg0
  Register #(.width(4)) u_Reg0 (.D(Data_In), .en(Write_Reg0), .Q(Reg0), .clk(CLK));  // open: clr
  // Probe on Reg4
  Register #(.width(4)) u_Reg4 (.D(Data_In), .en(Write_Reg4), .Q(Reg4), .clk(CLK));  // open: clr
  // Probe on Reg8
  Register #(.width(4)) u_Reg8 (.D(Data_In), .en(Write_Reg8), .Q(Reg8), .clk(CLK));  // open: clr
  // Probe on Reg12
  Register #(.width(4)) u_Reg12 (.D(Data_In), .en(Write_Reg12), .Q(Reg12), .clk(CLK));  // open: clr
  // Probe on Reg1
  Register #(.width(4)) u_Reg1 (.D(Data_In), .en(Write_Reg1), .Q(Reg1), .clk(CLK));  // open: clr
  // Probe on Reg5
  Register #(.width(4)) u_Reg5 (.D(Data_In), .en(Write_Reg5), .Q(Reg5), .clk(CLK));  // open: clr
  // Probe on Reg9
  Register #(.width(4)) u_Reg9 (.D(Data_In), .en(Write_Reg9), .Q(Reg9), .clk(CLK));  // open: clr
  // Probe on Reg13
  Register #(.width(4)) u_Reg13 (.D(Data_In), .en(Write_Reg13), .Q(Reg13), .clk(CLK));  // open: clr
  Register #(.width(4)) u_Reg2 (.D(Data_In), .en(Write_Reg2), .Q(Reg2), .clk(CLK));  // open: clr
  Register #(.width(4)) u_Reg6 (.D(Data_In), .en(Write_Reg6), .Q(Reg6), .clk(CLK));  // open: clr
  Register #(.width(4)) u_Reg10 (.D(Data_In), .en(Write_Reg10), .Q(Reg10), .clk(CLK));  // open: clr
  Register #(.width(4)) u_Reg14 (.D(Data_In), .en(Write_Reg14), .Q(Reg14), .clk(CLK));  // open: clr
  // Probe on Reg2
  // Probe on Reg6
  // Probe on Reg10
  // Probe on Reg14
  // Probe on Reg3
  Register #(.width(4)) u_Reg3 (.D(Data_In), .en(Write_Reg3), .Q(Reg3), .clk(CLK));  // open: clr
  // Probe on Reg7
  Register #(.width(4)) u_Reg7 (.D(Data_In), .en(Write_Reg7), .Q(Reg7), .clk(CLK));  // open: clr
  // Probe on Reg11
  Register #(.width(4)) u_Reg11 (.D(Data_In), .en(Write_Reg11), .Q(Reg11), .clk(CLK));  // open: clr
  // Probe on Reg15
  Register #(.width(4)) u_Reg15 (.D(Data_In), .en(Write_Reg15), .Q(Reg15), .clk(CLK));  // open: clr
  Multiplexer #(.select(4), .width(4), .enable("false")) multiplexer_1 (
    .in0(Reg0), .in1(Reg1), .in2(Reg2), .in3(Reg3), .in4(Reg4), .in5(Reg5), .in6(Reg6), .in7(Reg7),
    .in8(Reg8), .in9(Reg9), .in10(Reg10), .in11(Reg11), .in12(Reg12), .in13(Reg13), .in14(Reg14),
    .in15(Reg15), .out(A_DATA), .sel(A));
  Multiplexer #(.select(4), .width(4), .enable("false")) multiplexer_2 (
    .in0(Reg0), .in1(Reg1), .in2(Reg2), .in3(Reg3), .in4(Reg4), .in5(Reg5), .in6(Reg6), .in7(Reg7),
    .in8(Reg8), .in9(Reg9), .in10(Reg10), .in11(Reg11), .in12(Reg12), .in13(Reg13), .in14(Reg14),
    .in15(Reg15), .out(B_DATA), .sel(B));
endmodule
