// Logisim project 4bitAdder.circ as structural Verilog: 8 circuits, main circuit main
// Number Correct
module main (
  input  Enable_Halt
);

  wire and_2_out, CLK, Correct, Halt, not_1_out, not_2_out, NotDone, YourCout;
  wire [3:0] A, B, YourSum;
  wire [4:0] Solution;
  wire [8:0] Number_Correct_q;

  not not_1 (not_1_out, Correct);
  and and_1 (Halt, Enable_Halt, not_1_out);
  Clock clock_1 (.out(CLK));
  Inputs inputs_1 (.Halt(Halt), .Clk(CLK), .A(A), .B(B), .NotDone(NotDone));
  // Probe on A
  // Probe on B
  // Probe on YourSum
  // Probe on YourCout
  // Probe on Solution[3:0]
  // Probe on Solution[4]
  _4bitAdder _4BitAdder (.A(A), .B(B), .Cin(1'b0), .Sum(YourSum), .Cout(YourCout));
  not not_2 (not_2_out, Halt);
  and and_2 (and_2_out, Correct, NotDone, not_2_out);
  Checker checker_1 (.A(A), .B(B), .Sum(YourSum), .Cout(YourCout), .Correct(Correct), .CorrectAnswer(Solution));
  Counter #(.width(9), .max('h100)) Number_Correct (
    .count(and_2_out), .Q(Number_Correct_q), .clk(CLK));  // open: load, D, carry, clr
  // Probe on Number_Correct_q

  // Notes on the sheet:
  //   Use the Poke Tool on the enable halt input to enable/disable halting
  //   Enabling Halt will cause the testing to stop as soon as the first incorrect answer is detected
endmodule

module _4bitAdder (
  input  [3:0] A,
  input  [3:0] B,
  input  Cin,
  output [3:0] Sum,
  output Cout
);

  wire and_1_out, and_2_out, and_3_out, and_4_out, and_5_out, C1, C2, C3, G0, G1, G2, G3, or_2_out, or_3_out,
       or_4_out, P0, P1, P2, P3;

  or or_1 (Cout, or_2_out, and_1_out);
  and and_1 (and_1_out, and_5_out, Cin);
  or or_2 (or_2_out, G3, and_2_out);
  and and_2 (and_2_out, P3, or_3_out);
  or or_3 (or_3_out, G2, and_3_out);
  and and_3 (and_3_out, P2, or_4_out);
  or or_4 (or_4_out, G1, and_4_out);
  Pi pi_1 (.Ai(A[0]), .Bi(B[0]), .Pi(P0));
  Pi pi_2 (.Ai(A[1]), .Bi(B[1]), .Pi(P1));
  Pi pi_3 (.Ai(A[2]), .Bi(B[2]), .Pi(P2));
  Pi pi_4 (.Ai(A[3]), .Bi(B[3]), .Pi(P3));
  Gi gi_1 (.Ai(A[0]), .Bi(B[0]), .Gi(G0));
  Gi gi_2 (.Ai(A[1]), .Bi(B[1]), .Gi(G1));
  Gi gi_3 (.Ai(A[2]), .Bi(B[2]), .Gi(G2));
  Gi gi_4 (.Ai(A[3]), .Bi(B[3]), .Gi(G3));
  Ci ci_1 (.Gi(G0), .Pi(P0), .CI(Cin), .Ci_2(C1));
  Ci ci_2 (.Gi(G1), .Pi(P1), .CI(C1), .Ci_2(C2));
  Ci ci_3 (.Gi(G2), .Pi(P2), .CI(C2), .Ci_2(C3));
  and and_4 (and_4_out, P1, G0);
  and and_5 (and_5_out, P1, P2, P3, P0);
  Si si_1 (.Pi(P0), .Ci(Cin), .Si(Sum[0]));
  Si si_2 (.Pi(P1), .Ci(C1), .Si(Sum[1]));
  Si si_3 (.Pi(P2), .Ci(C2), .Si(Sum[2]));
  Si si_4 (.Pi(P3), .Ci(C3), .Si(Sum[3]));

  // Other names for the same wires on the sheet: S0 = Sum[0]; S1 = Sum[1]; S2 = Sum[2]; S3 = Sum[3]
endmodule

module Inputs (
  input  Halt,
  input  Clk,
  output [3:0] A,
  output [3:0] B,
  output NotDone
);

  wire A_carry, and_1_out, and_2_out, and_3_out, and_4_out, CarryB, Delay_q, nHalt;

  not not_1 (nHalt, Halt);
  and and_1 (and_1_out, nHalt, NotDone);
  Counter #(.width(4), .max('hf)) u_B (.count(and_1_out), .Q(B), .carry(CarryB), .clk(Clk));  // open: load, D, clr
  and and_2 (and_2_out, nHalt, CarryB);
  Counter #(.width(4), .max('hf), .ongoal("stay")) u_A (
    .count(and_2_out), .Q(A), .carry(A_carry), .clk(Clk));  // open: load, D, clr
  and and_3 (and_3_out, CarryB, A_carry);
  Register #(.width(1)) Delay (.D(and_3_out), .en(and_4_out), .Q(Delay_q), .clk(Clk));  // open: clr
  and and_4 (and_4_out, nHalt, NotDone);
  not not_2 (NotDone, Delay_q);
endmodule

module Checker (
  input  [3:0] A,
  input  [3:0] B,
  input  [3:0] Sum,
  input  Cout,
  output Correct,
  output [4:0] CorrectAnswer
);

  ROM #(.dataWidth(5)) rom_1 (.addr({A, B}), .data(CorrectAnswer));  // open: sel
  Comparator #(.width(5), .mode("unsigned")) comparator_1 (
    .a(CorrectAnswer), .b({Cout, Sum}), .eq(Correct));  // open: gt, lt

  // Other names for the same wires on the sheet: StudentSol[4:0] = {Cout, Sum}

  // Notes on the sheet:
  //   contents of rom_1 (hex, n*v repeats v):
  //   0 1 2 3 4 5 6 7 8 9 a b c d e f 1 2 3 4 5 6 7 8 9 a b c d e f 10 2 3 4 5 6 7 8 9 a b c d e f 10 11 3
  //   4 5 6 7 8 9 a b c d e f 10 11 12 4 5 6 7 8 9 a b c d e f 10 11 12 13 5 6 7 8 9 a b c d e f 10 11 12
  //   13 14 6 7 8 9 a b c d e f 10 11 12 13 14 15 7 8 9 a b c d e f 10 11 12 13 14 15 16 8 9 a b c d e f
  //   10 11 12 13 14 15 16 17 9 a b c d e f 10 11 12 13 14 15 16 17 18 a b c d e f 10 11 12 13 14 15 16 17
  //   18 19 b c d e f 10 11 12 13 14 15 16 17 18 19 1a c d e f 10 11 12 13 14 15 16 17 18 19 1a 1b d e f
  //   10 11 12 13 14 15 16 17 18 19 1a 1b 1c e f 10 11 12 13 14 15 16 17 18 19 1a 1b 1c 1d f 10 11 12 13
  //   14 15 16 17 18 19 1a 1b 1c 1d 1e
endmodule

module Pi (
  input  Ai,
  input  Bi,
  output Pi
);

  xor xor_1 (Pi, Ai, Bi);
endmodule

module Gi (
  input  Ai,
  input  Bi,
  output Gi
);

  and and_1 (Gi, Ai, Bi);
endmodule

module Si (
  input  Pi,
  input  Ci,
  output Si
);

  xor xor_1 (Si, Pi, Ci);
endmodule

module Ci (
  input  Gi,
  input  Pi,
  input  CI,
  output Ci_2
);

  wire and_1_out;

  and and_1 (and_1_out, Pi, CI);
  or or_1 (Ci_2, Gi, and_1_out);
endmodule
